# Fritzing sketch speaker (saved by Fritzing 0.9.4)
breadboards: 1

parts:
  Part1 = Arduino Uno (Rev3)
  S1 = Momentary Switch [package=ksa_sealed_tac_switch]
  SP1 = SPEAKER [package=pcb_mount_speaker]

nets:
  N1: Part1.D9_PWM, SP1.-
  N2: Part1.GND, S1.4, SP1.+
  N3: Part1.RESET, S1.2
